# Fritzing sketch sketch2 (saved by Fritzing 0.9.3b)
breadboards: 1

parts:
  Part1 = Arduino Uno (Rev3)
  U2 = ESP8266 WiFi Module [part_number=ESP8266]
  U1 = Sharp Dust Sensor [part_number=GP2Y1010AU0F]
  R1 = Resistor [package="2512 [SMD]"]
  C1 = Capacitor Polarized [package=cpol-radial-10uf-25v]
  LCD1 = LCD screen
  R2 = Resistor [package="2512 [SMD]"]

nets:
  N1: Part1.A5/SCL, U1.Vo
  N2: Part1.D10_PWM/SS, U2.RXD
  N3: Part1.D11_PWM/MOSI, U2.TXD
  N4: Part1.D12/MISO, U1.LED
  GND: Part1.GND, U2.GND, U1.LED-GND, U1.S-GND, C1.-, LCD1.VSS
  N5: Part1.D2, LCD1.RS
  N6: Part1.D3_PWM, LCD1.E
  N7: Part1.D4, LCD1.DB4
  N8: Part1.D5_PWM, LCD1.DB5
  N9: Part1.D6_PWM, LCD1.DB6
  N10: Part1.D7, LCD1.DB7
  3V3: Part1.3V3, U2.VCC, U2.CH_PD
  5V: Part1.5V, U1.VCC, R1.Pin_1, LCD1.VDD, R2.Pin_1
  N11: U1.V-LED, R1.Pin_0, C1.+, R2.Pin_0

custom parts:
  ESP8266 WiFi Module: Generic WiFi Module based on the ESP8266 with onboard PCB antenna and UART communications
  Sharp Dust Sensor: Sharp GP2Y1010AU0F Dust Sensor
  Resistor: Resistor Basic schematic elements and footprints for 0603, 1206, and PTH resistors.
